// Logisim project aula_1.circ as structural Verilog: 1 circuit, main circuit main
module main (
  input  [31:0] in_1,
  input  [3:0] ALU_OP,
  input  CONTROLE,
  output [5:0] FUNCT,
  output [4:0] S_A
);

  wire CLOCK_out, registerfile_1_p1, registerfile_1_p7, registerfile_1_p8;
  wire [31:11] mipsprogramrom_1_p2;

  // MIPSProgramROM mipsprogramrom_1: pin names not known; wires that end beside it: in_1, {mipsprogramrom_1_p2, S_A, FUNCT}
  Clock CLOCK (.out(CLOCK_out));
  // RegisterFile registerfile_1: pin names not known; wires that end beside it: registerfile_1_p1, CLOCK_out, CONTROLE, mipsprogramrom_1_p2[15:11], mipsprogramrom_1_p2[25:21], mipsprogramrom_1_p2[20:16], registerfile_1_p7, registerfile_1_p8
  // Mips_ALU mips_alu_1: pin names not known; wires that end beside it: registerfile_1_p7, registerfile_1_p8, ALU_OP, registerfile_1_p1

  // Notes on the sheet:
  //   DADO
  //   END
  //   END
  //   END
  //   DADO
  //   DADO
  //   SOMA
endmodule
