// Logisim project projeto_II.circ as structural Verilog: 2 circuits, main circuit main
module main (
  input  in_1,
  output out_2
);

  wire ALU_SRC, CLK, LOAD, MEM_TO_REG, REG_DEST, REG_W, registerfile_1_p7, RESET, STORE;
  wire [3:0] ALU_OP;
  wire [4:0] multiplexer_1_out;
  wire [5:0] FUNCT, OPCODE;
  wire [25:6] mipsprogramrom_1_p2;
  wire [31:0] adder_1_out, bit_extender_1_out, mips_alu_1_p2, mips_alu_1_p4, mips_ram_1_p7, register_1_q,
       registerfile_1_p1, registerfile_1_p8;

  Register #(.width(32)) register_1 (.D(adder_1_out), .Q(register_1_q), .clk(CLK));  // open: en, clr
  Adder #(.width(32)) adder_1 (.a(register_1_q), .b(32'h4), .out(adder_1_out));  // open: cin, cout
  Clock clock_1 (.out(CLK));
  control control_1 (
    .OPCODE(OPCODE), .unidades_de_controle_desativadas(in_1), .REG_DEST(REG_DEST), .REG_W(REG_W),
    .ALU_SRC(ALU_SRC), .MEM_TO_REG(MEM_TO_REG), .LOAD(LOAD), .STORE(STORE), .RESET(RESET), .ALU_OP(ALU_OP));
  // MIPSProgramROM mipsprogramrom_1: pin names not known; wires that end beside it: register_1_q, {OPCODE, mipsprogramrom_1_p2, FUNCT}
  Multiplexer #(.width(5), .enable("false")) multiplexer_1 (
    .in0(mipsprogramrom_1_p2[15:11]), .in1(mipsprogramrom_1_p2[20:16]), .out(multiplexer_1_out),
    .sel(REG_DEST));
  // RegisterFile registerfile_1: pin names not known; wires that end beside it: registerfile_1_p1, CLK, REG_W, multiplexer_1_out, mipsprogramrom_1_p2[25:21], mipsprogramrom_1_p2[20:16], registerfile_1_p7, registerfile_1_p8
  assign bit_extender_1_out = {{16{1'b0}}, {mipsprogramrom_1_p2[15:6], FUNCT}};  // Bit_Extender bit_extender_1
  // Mips_ALU mips_alu_1: pin names not known; wires that end beside it: registerfile_1_p7, mips_alu_1_p2, ALU_OP, mips_alu_1_p4
  Multiplexer #(.width(32), .enable("false")) multiplexer_2 (
    .in0(registerfile_1_p8), .in1(bit_extender_1_out), .out(mips_alu_1_p2), .sel(ALU_SRC));
  // MIPS_RAM mips_ram_1: pin names not known; wires that end beside it: mips_alu_1_p4[19:0], registerfile_1_p8, STORE, CLK, LOAD, RESET, mips_ram_1_p7
  Multiplexer #(.width(32), .enable("false")) multiplexer_3 (
    .in0(mips_alu_1_p4), .in1(mips_ram_1_p7), .out(registerfile_1_p1), .sel(MEM_TO_REG));

  // Other names for the same wires on the sheet: SUBU = out_2

  // Notes on the sheet:
  //   tipo R
  //   tipo I
  //   (controle)
  //   END
  //   END
  //   END
  //   DADO
  //   DESTINO
  //   ORIGEM 2
  //   ORIGEM 1
  //   DADO
  //   tipo R
  //   tipo I
  //   SOMA
  //   0010 - SOMA
  //   0110 - SUB
endmodule

module control (
  input  [5:0] OPCODE,
  input  unidades_de_controle_desativadas,
  output REG_DEST,
  output REG_W,
  output ALU_SRC,
  output [3:0] ALU_OP,
  output MEM_TO_REG,
  output LOAD,
  output STORE,
  output RESET
);

  wire ADDIU, ORI;

  and and_1 (ADDIU, OPCODE[0], ~OPCODE[1], ~OPCODE[2], OPCODE[3], ~OPCODE[4], ~OPCODE[5]);  // AND_Gate
  and and_2 (ORI, OPCODE[0], ~OPCODE[1], OPCODE[2], OPCODE[3], ~OPCODE[4], ~OPCODE[5]);  // AND_Gate
  Multiplexer #(.width(4), .enable("false")) multiplexer_1 (.in0(4'b0010), .in1(4'b1101), .out(ALU_OP), .sel(ORI));
  or or_1 (REG_DEST, ADDIU, ORI);
  or or_2 (REG_W, ADDIU, ORI);
  or or_3 (ALU_SRC, ADDIU, ORI);

  assign LOAD = unidades_de_controle_desativadas;
  assign MEM_TO_REG = unidades_de_controle_desativadas;
  assign RESET = unidades_de_controle_desativadas;
  assign STORE = unidades_de_controle_desativadas;

  // Notes on the sheet:
  //   0010
endmodule
