// Logisim project tipoR_tipoI.circ as structural Verilog: 1 circuit, main circuit main
module main (
  input  in_1,
  output out_2,
  output out_3,
  output out_4
);

  wire and_2_out, and_3_out, and_4_out, CLK, REG_W, registerfile_1_p7;
  wire [3:0] ALU_OP;
  wire [4:0] multiplexer_1_out;
  wire [5:0] FUNCT, OPCODE;
  wire [25:6] mipsprogramrom_1_p2;
  wire [31:0] adder_1_out, bit_extender_1_out, mips_alu_1_p2, mips_alu_1_p4, mips_ram_1_p7, register_1_q,
       registerfile_1_p1, registerfile_1_p8;

  Register #(.width(32)) register_1 (.D(adder_1_out), .Q(register_1_q), .clk(CLK));  // open: en, clr
  Adder #(.width(32)) adder_1 (.a(register_1_q), .b(32'h4), .out(adder_1_out));  // open: cin, cout
  and and_1 (out_2, OPCODE[0], ~OPCODE[1], ~OPCODE[2], OPCODE[3], ~OPCODE[4], ~OPCODE[5]);  // AND_Gate
  and and_2 (and_2_out, ~OPCODE[0], ~OPCODE[1], ~OPCODE[2], ~OPCODE[3], ~OPCODE[4], ~OPCODE[5]);  // AND_Gate
  and and_3 (and_3_out, FUNCT[0], ~FUNCT[1], ~FUNCT[2], ~FUNCT[3], ~FUNCT[4], FUNCT[5]);  // AND_Gate
  and and_4 (and_4_out, FUNCT[0], FUNCT[1], ~FUNCT[2], ~FUNCT[3], ~FUNCT[4], FUNCT[5]);  // AND_Gate
  and and_5 (out_3, and_2_out, and_3_out);
  and and_6 (out_4, and_2_out, and_4_out);
  // MIPSProgramROM mipsprogramrom_1: pin names not known; wires that end beside it: register_1_q, {OPCODE, mipsprogramrom_1_p2, FUNCT}
  Multiplexer #(.width(5), .enable("false")) multiplexer_1 (
    .in0(mipsprogramrom_1_p2[15:11]), .in1(mipsprogramrom_1_p2[20:16]), .out(multiplexer_1_out), .sel(out_2));
  Multiplexer #(.width(4), .enable("false")) multiplexer_2 (.in0(4'b0010), .in1(4'b0110), .out(ALU_OP), .sel(out_4));
  Clock CLOCK (.out(CLK));
  or or_1 (REG_W, out_2, out_3, out_4);
  // RegisterFile registerfile_1: pin names not known; wires that end beside it: registerfile_1_p1, CLK, REG_W, multiplexer_1_out, mipsprogramrom_1_p2[25:21], mipsprogramrom_1_p2[20:16], registerfile_1_p7, registerfile_1_p8
  assign bit_extender_1_out = {{16{1'b0}}, {mipsprogramrom_1_p2[15:6], FUNCT}};  // Bit_Extender bit_extender_1
  // Mips_ALU mips_alu_1: pin names not known; wires that end beside it: registerfile_1_p7, mips_alu_1_p2, ALU_OP, mips_alu_1_p4
  Multiplexer #(.width(32), .enable("false")) multiplexer_3 (
    .in0(registerfile_1_p8), .in1(bit_extender_1_out), .out(mips_alu_1_p2), .sel(out_2));
  // MIPS_RAM mips_ram_1: pin names not known; wires that end beside it: mips_alu_1_p4[19:0], registerfile_1_p8, in_1, CLK, in_1, in_1, mips_ram_1_p7
  Multiplexer #(.width(32), .enable("false")) multiplexer_4 (
    .in0(mips_alu_1_p4), .in1(mips_ram_1_p7), .out(registerfile_1_p1), .sel(in_1));

  // Other names for the same wires on the sheet: ADDU = out_3; ADDIU = out_2; ALU_SRC = out_2; REG_DEST = out_2;
  //   LOAD = in_1; MEM_TO_REG = in_1; RESET = in_1; STORE = in_1; SUBU = out_4

  // Notes on the sheet:
  //   tipo R
  //   tipo I
  //   (controle)
  //   END
  //   END
  //   END
  //   0010
  //   DADO
  //   DESTINO
  //   0110
  //   ORIGEM 2
  //   ORIGEM 1
  //   DADO
  //   tipo R
  //   tipo I
  //   SOMA
  //   0010 - SOMA
  //   0110 - SUB
endmodule
